# Fritzing sketch GPS Clock (saved by Fritzing 0.9.3b)
breadboards: 1

parts:
  Arduino = Arduino Nano (Rev3.0)
  Temp_Sensor = Humidity and Temperature Sensor RHT03
  Real_Time_Cock = Real Time Clock Module - DS1307 RTC Breakout Board
  BSC_Button = Momentary Switch [package=ksa_sealed_tac_switch]
  SSC_Button = Momentary Switch [package=ksa_sealed_tac_switch]
  A_Button = Momentary Switch [package=ksa_sealed_tac_switch]
  B_Button = Momentary Switch [package=ksa_sealed_tac_switch]
  GPS_(NEO-6M) = SUP500F [package=sup500f]
  Small_Display = 14-segment LED Alphanumeric Backpack [part_number=2158]
  Big_Display = Seven-Segment LED Backpack 1.2 Inch Digits [part_number=1269]
  R1 = Resistor [tolerance=±5% resistance=10k package=THT]
  R2 = Resistor [tolerance=±5% resistance=10k package=THT]
  R3 = Resistor [tolerance=±5% resistance=10k package=THT]
  R4 = Resistor [tolerance=±5% resistance=10k package=THT]
  R5 = Resistor [tolerance=±5% resistance=10k package=THT]
  R6 = Resistor [tolerance=±5% resistance=10k package=THT]
  R7 = Resistor [tolerance=±5% resistance=10k package=THT]
  Light_Sensor = Photocell (LDR) [package=THT]
  J1 = Piezo Speaker
  R8 = Resistor [tolerance=±5% resistance=10k package=THT]
  R9 = Resistor [tolerance=±5% resistance=100 package=THT]

nets:
  N1: Arduino.D3, BSC_Button.2
  N2: Arduino.D4, SSC_Button.2
  N3: Arduino.D5, A_Button.2
  N4: Arduino.D6, B_Button.2
  N5: Arduino.D7, Temp_Sensor.Data-signal, R5.Pin_1
  N6: Arduino.D9, R9.Pin_1
  N7: Arduino.D10, GPS_(NEO-6M).TX-O
  N8: Arduino.D11/MOSI, GPS_(NEO-6M).RX-I
  N9: Arduino.A5, Real_Time_Cock.SCL, Small_Display.SCL, Big_Display.SCL, R7.Pin_0
  N10: Arduino.A4, Real_Time_Cock.SDA, Small_Display.SDA, Big_Display.SDA, R6.Pin_0
  N11: Arduino.A0, Light_Sensor.pin_0, R8.Pin_1
  N12: Temp_Sensor.Vcc, R5.Pin_0
  GND: Temp_Sensor.GND_2, Real_Time_Cock.GND, GPS_(NEO-6M).GND, Small_Display.GND, Big_Display.GND, R1.Pin_0, R2.Pin_0, R3.Pin_0, R4.Pin_0, R6.Pin_1, R7.Pin_1, J1.pin1, R8.Pin_0
  5V: Real_Time_Cock.5V, BSC_Button.3, SSC_Button.3, A_Button.3, B_Button.3, GPS_(NEO-6M).VCC, Small_Display.VDD, Small_Display.VI2C, Big_Display.VDD, Big_Display.VCCIO, Light_Sensor.pin_1
  N13: BSC_Button.1, R4.Pin_1
  N14: SSC_Button.1, R3.Pin_1
  N15: A_Button.1, R2.Pin_1
  N16: B_Button.1, R1.Pin_1
  N17: J1.pin2, R9.Pin_0

notes:
  Purple: RX Signal
  Blue: TX Signal
  Cyan: Analog Input
  Orange: 2-Way Data
  Yellow: Clock

custom parts:
  14-segment LED Alphanumeric Backpack: This is a nice, bright alphanumeric display that shows letters and numbers. It's super bright and designed for viewing from distances up to 23 feet (7 meters) away. Four digits with 14 segments on a black surface and we give you a set of two alphanumeric displays as well as a driver board so you can make a clock or a four letter word. Like our other LED backpacks, these are end-to-end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
  Seven-Segment LED Backpack 1.2 Inch Digits: This jumbo 1.2" 7-segment LED display includes a driver chip for simple control via an I2C interface. The backpack features address-selection jumpers so you can connect up to eight displays on a single I2C bus.
